# Fritzing sketch Pi Gas Module (saved by Fritzing 0.9.4)
circuit board: 8.49119cm x 9.44518cm
breadboards: 1

parts:
  MCU1 = Raspberry Pi Zero
  U1 = GAS_SENSOR [package=mq-3]
  ADC1 = MCP3008 [package=dil16]
  LED2 = LED - 5mm [color="Red (633nm)" package="5 mm [THT]"]
  LED3 = LED - 5mm [color="Green (570nm)" package="5 mm [THT]"]
  R5 = Resistor [tolerance=±5% resistance=220 package="2512 [SMD]"]
  R6 = Resistor [tolerance=±5% resistance=220 package="2512 [SMD]"]
  R8 = Resistor [tolerance=±5% resistance=10k package="2512 [SMD]"]
  S1 = Momentary Switch [package=ksa_sealed_tac_switch]
  S2 = Momentary Switch [package=ksa_sealed_tac_switch]
  S3 = Momentary Switch [package=ksa_sealed_tac_switch]
  R10 = Resistor [tolerance=±5% resistance=10k package="2512 [SMD]"]
  R11 = Resistor [tolerance=±5% resistance=10k package="2512 [SMD]"]
  LCD1 = LCD screen
  Part1 = Logic Level Converter
  J1 = Piezo Speaker

nets:
  N1: MCU1.pin_1, ADC1.VREF, ADC1.VDD, Part1.LV
  N2: MCU1.pin_2, LCD1.VDD, Part1.HV
  VSS: MCU1.pin_6, MCU1.pin_20, MCU1.pin_25, U1.A1, ADC1.DGND, ADC1.AGND, R5.Pin_1, R6.Pin_1, R8.Pin_1, R10.Pin_1, R11.Pin_1, LCD1.VSS, LCD1.V0, LCD1.R/W, Part1.GND, J1.pin1
  N3: MCU1.pin_11, LED2.anode
  N4: MCU1.pin_13, LED3.anode
  N5: MCU1.pin_15, J1.pin2
  N6: MCU1.pin_16, S1.2
  N7: MCU1.pin_18, S2.2
  N8: MCU1.pin_19, ADC1.Din
  N9: MCU1.pin_21, ADC1.Dout
  N10: MCU1.pin_22, S3.2
  N11: MCU1.pin_23, ADC1.CLK
  N12: MCU1.pin_24, ADC1.CS/SHDN
  N13: MCU1.pin_29, LCD1.DB6
  N14: MCU1.pin_31, LCD1.DB5
  N15: MCU1.pin_33, LCD1.DB4
  N16: MCU1.pin_35, LCD1.E
  N17: MCU1.pin_36, LCD1.DB7
  N18: MCU1.pin_37, LCD1.RS
  N19: U1.B1, Part1.RX2_HV
  N20: ADC1.CH0, Part1.RX2_LV
  N21: LED2.cathode, R5.Pin_0
  N22: LED3.cathode, R6.Pin_0
  N23: R8.Pin_0, S1.4
  N24: S2.4, R10.Pin_0
  N25: S3.4, R11.Pin_0
